# Fritzing sketch Untitled Sketch (saved by Fritzing 1.0.5)

parts:
  Part1 = Arduino Uno (Rev3)
  KY-1 = Keyes Relay [package=THT]
  R1 = Resistor [tolerance=±5% power=0.25W resistance=220 package=THT]
  LED1 = LED - 5mm [color="Red (633nm)" current=0.030A package="5 mm [THT]"]

nets (from the schematic view):
  N1: Part1.GND, KY-1.power, R1.Pin_0
  N2: Part1.D6_PWM, KY-1.ground
  N3: KY-1.signal, KY-1.C, KY-1.NO, LED1.anode
  N4: R1.Pin_1, LED1.cathode

custom parts:
  Keyes Relay: The Keyes 5V relay module is suitable for SCM development, home appliance control. It uses a 5V~12V TIL control signal which can control DC / AC signal.
